# Fritzing sketch skematik (saved by Fritzing 0.9.3b)

parts:
  MH-ET_LIVE_ESP32_DEVKIT1 = MH-ET LIVE ESP32 DEVKIT 38 pins
  F1 = Small Fan, based on Fan - Ventilador [package=THT]
  KY-1 = Keyes Relay [package=THT]
  DHT1 = DHT11 Humitidy and Temperature Sensor (3 pins)
  Part1 = LCD1602-I2C
  VCC1 = Battery block 9V

nets:
  3V3: MH-ET_LIVE_ESP32_DEVKIT1.3V3, Part1.VCC
  GND: MH-ET_LIVE_ESP32_DEVKIT1.GND, KY-1.ground, Part1.GND
  N1: MH-ET_LIVE_ESP32_DEVKIT1.IO23, KY-1.power
  N2: MH-ET_LIVE_ESP32_DEVKIT1.IO22, Part1.SCL
  N3: MH-ET_LIVE_ESP32_DEVKIT1.IO21, Part1.SDA
  N4: MH-ET_LIVE_ESP32_DEVKIT1.IO5, DHT1.Signal
  N5: F1.5V, KY-1.C
  N6: F1.GND, VCC1.-
  N7: KY-1.NO, VCC1.+

custom parts:
  MH-ET LIVE ESP32 DEVKIT 38 pins: http://mh.nodebb.com/topic/2/mh-et-live-esp32-devkit
  Small Fan, based on Fan - Ventilador: Small 2-pin fan, commonly used with single-board computers, 3d-printers, etc. This work is based on a much larger fan, as commonly found in desktop computers
  Keyes Relay: The Keyes 5V relay module is suitable for SCM development, home appliance control. It uses a 5V~12V TIL control signal which can control DC / AC signal.
  DHT11 Humitidy and Temperature Sensor (3 pins): DHT11 Humidity and Temperature Sensor (3 pins).
  LCD1602-I2C: A standard character display, usually with 2x16 characters. Comes in many colors with LCM1602 IIC attached.
  Battery block 9V: 9 Volt battery block with 200mil pcb footprint spacing
